// Logisim project ringcouter4.circ as structural Verilog: 1 circuit, main circuit main
module main (
  input  MainClock,
  input  Clear,
  output [3:0] Phase
);

  wire d_ff_1_q, d_ff_1_qn, d_ff_2_q, d_ff_3_q, d_ff_4_q, d_ff_4_qn, not_1_out, not_2_out, not_3_out,
       not_4_out;

  xor xor_1 (Phase[0], d_ff_4_q, d_ff_1_qn);
  D_Flip_Flop #(.trigger("falling")) d_ff_1 (
    .D(d_ff_4_qn), .clk(MainClock), .Q(d_ff_1_q), .Qn(d_ff_1_qn), .reset(not_1_out));  // open: preset
  not not_1 (not_1_out, Clear);
  xor xor_2 (Phase[1], d_ff_1_q, d_ff_2_q);
  D_Flip_Flop #(.trigger("falling")) d_ff_2 (
    .D(d_ff_1_q), .clk(MainClock), .Q(d_ff_2_q), .reset(not_2_out));  // open: Qn, preset
  not not_2 (not_2_out, Clear);
  xor xor_3 (Phase[2], d_ff_2_q, d_ff_3_q);
  D_Flip_Flop #(.trigger("falling")) d_ff_3 (
    .D(d_ff_2_q), .clk(MainClock), .Q(d_ff_3_q), .reset(not_3_out));  // open: Qn, preset
  not not_3 (not_3_out, Clear);
  xor xor_4 (Phase[3], d_ff_3_q, d_ff_4_q);
  D_Flip_Flop #(.trigger("falling")) d_ff_4 (
    .D(d_ff_3_q), .clk(MainClock), .Q(d_ff_4_q), .Qn(d_ff_4_qn), .reset(not_4_out));  // open: preset
  not not_4 (not_4_out, Clear);

  // Other names for the same wires on the sheet: Phase_Count = MainClock

  // Notes on the sheet:
  //   Inputs
  //   Outputs
  //   Ring Counter 4Bits Circuit
endmodule
